# Fritzing sketch buzzer_fritzing (saved by Fritzing 0.9.4)
breadboards: 1

parts:
  Part1 = Arduino Uno (Rev3)
  J1 = Piezo Speaker
  R1 = Resistor [tolerance=±5% resistance=100 package=THT]

nets:
  N1: Part1.D12/MISO, J1.pin2
  N2: Part1.GND, R1.Pin_0
  N3: J1.pin1, R1.Pin_1
